# Fritzing sketch M6BoKijkdoos (saved by Fritzing 0.9.3b)
breadboards: 1

parts:
  Part1 = Arduino Uno (Rev3) - ICSP
  R1 = Resistor [tolerance=±5% resistance=220 package=THT]
  R2 = Resistor [tolerance=±5% resistance=220 package=THT]
  R3 = Resistor [tolerance=±5% resistance=220 package=THT]
  J1 = Basic Servo
  J2 = Basic Servo
  J3 = Basic Servo
  J4 = Basic Servo
  J5 = Basic Servo
  J6 = Basic Servo
  LED1 = LED - 5mm [color="Red (633nm)" package="5 mm [THT]"]
  LED2 = LED - 5mm [color="Red (633nm)" package="5 mm [THT]"]
  LED3 = LED - 5mm [color="Red (633nm)" package="5 mm [THT]"]
  LED4 = LED - 5mm [color="Red (633nm)" package="5 mm [THT]"]
  LED5 = LED - 5mm [color="Red (633nm)" package="5 mm [THT]"]
  LED6 = LED - 5mm [color="Red (633nm)" package="5 mm [THT]"]
  R4 = Photocell (LDR) [package=THT]
  Power_plug1 = Power plug
  C1 = Electrolytic Capacitor [capacitance=1µF package="100 mil [THT, electrolytic]"]

nets:
  N1: Part1.D8, J4.pulse
  N2: Part1.D10_PWM/SS, J2.pulse
  N3: Part1.D11_PWM/MOSI, J1.pulse
  N4: Part1.D12/MISO, J5.pulse
  N5: Part1.D13/SCK, J6.pulse
  N6: R1.Pin_0, LED1.anode, LED2.anode
  VCC: R1.Pin_1, R2.Pin_1, R3.Pin_1, J1.vcc, J2.vcc, J3.vcc, J4.vcc, J5.vcc, R4.pin_0, Power_plug1.VCC, C1.-
  N7: R2.Pin_0, LED3.anode, LED5.anode
  N8: R3.Pin_0, LED4.anode, LED6.anode
  GND: J1.gnd, J2.gnd, J3.gnd, J4.gnd, J5.gnd, J6.gnd, LED1.cathode, LED2.cathode, LED3.cathode, LED4.cathode, LED5.cathode, LED6.cathode, Power_plug1.GND, C1.+

// code stored in the sketch: allCodeKijkdoos.ino
// Include the servo library:
#include "Servo.h"
#define SERVO_NUM 6

//create a new servo object 
Servo servoArray[SERVO_NUM]; //create array of servo object

//assign button to pin 7
#define BUTTON_PIN 7

//make buttonstate variable
int lastButtonState;

//connect pin to led
int LED_PIN0 = 1;
int LED_PIN1 = 2;
int LED_PIN2 = 3;
int LED_PIN3 = 4;

byte ledInArray[] = { LED_PIN0,
                      LED_PIN1,
                      LED_PIN2,
                      LED_PIN3 };

void setup() {
  //start serial monitor
  Serial.begin(115200);

 //servo
  // attach the servo variable to a pin:
  servoArray[1].attach(9);
  servoArray[2].attach(10);
  servoArray[3].attach(11);
  servoArray[4].attach(8);
  servoArray[5].attach(12);
  servoArray[6].attach(13);

  //button
  //enable internal pullup resistor
  pinMode(BUTTON_PIN, INPUT_PULLUP);
  lastButtonState = digitalRead(BUTTON_PIN);
  
  //LED
  //set pin output mode
  pinMode(LED_PIN1, OUTPUT);
  pinMode(LED_PIN2, OUTPUT);
  pinMode(LED_PIN3, OUTPUT);
}

void loop() {
  //button
  //read the value of the button
  int buttonState = digitalRead(BUTTON_PIN);

  //led
  if(lastButtonState != buttonState){ //state change
    delay(50); // debounce time

    if(buttonState == LOW){
      Serial.println("button pressed");
      //random
      for(int i = 0; i < 3; i++){
         int randomNumber = random(0,4);
         Serial.println(randomNumber);
         digitalWrite(ledInArray[randomNumber], HIGH);
      }
      delay(3000);
      for(int i = 0; i < ledInArray[i]; i++){
        digitalWrite(ledInArray[i], LOW);
      }  
    }
    lastButtonState = buttonState;
  }

}
